# Fritzing sketch redden_basis (saved by Fritzing 1.0.4)

parts:
  Arduino_Nano_Shield_V1 = Arduino Nano Shield V3
  Onderdeel1 = Arduino Nano RP2040 Connect
  Onderdeel2 = Arduino Nano RP2040 Connect
  Onderdeel3 = Arduino Nano RP2040 Connect
  Onderdeel4 = Arduino Nano RP2040 Connect
  Onderdeel5 = Arduino Nano RP2040 Connect
  Motor_Shield1 = Motor Shield Updated  # not connected
  I2C1 = I2C Updated  # not connected

nets:
  N1: Arduino_Nano_Shield_V1.D12, Onderdeel1.CIPO/D12/GPIO4, Onderdeel3.CIPO/D12/GPIO4, Onderdeel4.CIPO/D12/GPIO4
  N2: Arduino_Nano_Shield_V1.D11~, Onderdeel1.COPI/D11/GPIO7, Onderdeel2.CIPO/D12/GPIO4, Onderdeel3.COPI/D11/GPIO7, Onderdeel4.COPI/D11/GPIO7
  N3: Arduino_Nano_Shield_V1.D10~, Onderdeel1.D10/GPIO5, Onderdeel2.COPI/D11/GPIO7, Onderdeel3.D10/GPIO5, Onderdeel4.D10/GPIO5
  N4: Arduino_Nano_Shield_V1.D9~, Onderdeel1.D9/GPIO21, Onderdeel2.D10/GPIO5, Onderdeel3.D9/GPIO21, Onderdeel4.D9/GPIO21
  N5: Arduino_Nano_Shield_V1.D8, Onderdeel1.D8/GPIO20, Onderdeel2.D9/GPIO21, Onderdeel3.D8/GPIO20, Onderdeel4.D8/GPIO20
  N6: Arduino_Nano_Shield_V1.D7, Onderdeel1.D7/GPIO19, Onderdeel2.D8/GPIO20, Onderdeel3.D7/GPIO19, Onderdeel4.D7/GPIO19
  N7: Arduino_Nano_Shield_V1.D6~, Onderdeel1.D6/GPIO18, Onderdeel2.D7/GPIO19, Onderdeel3.D6/GPIO18, Onderdeel4.D6/GPIO18
  N8: Arduino_Nano_Shield_V1.D5~, Onderdeel1.D5/GPIO17, Onderdeel2.D6/GPIO18, Onderdeel3.D5/GPIO17, Onderdeel4.D5/GPIO17
  N9: Arduino_Nano_Shield_V1.D4, Onderdeel1.D4/GPIO16, Onderdeel2.D5/GPIO17, Onderdeel3.D4/GPIO16, Onderdeel4.D4/GPIO16
  N10: Arduino_Nano_Shield_V1.D3~, Onderdeel1.D3/GPIO15, Onderdeel2.D4/GPIO16, Onderdeel3.D3/GPIO15, Onderdeel4.D3/GPIO15
  N11: Arduino_Nano_Shield_V1.D2, Onderdeel1.D2/GPIO25, Onderdeel2.D3/GPIO15, Onderdeel3.D2/GPIO25, Onderdeel4.D2/GPIO25
  GND: Arduino_Nano_Shield_V1.GND, Onderdeel1.GND, Onderdeel2.QSPI_CSn/RESET, Onderdeel2.D2/GPIO25, Onderdeel3.GND, Onderdeel4.GND, Onderdeel5.GND
  VIN: Arduino_Nano_Shield_V1.RST#57, Arduino_Nano_Shield_V1.VIN, Onderdeel1.VIN, Onderdeel1.RESET, Onderdeel2.GND, Onderdeel3.VIN, Onderdeel3.RESET, Onderdeel4.VIN, Onderdeel4.RESET, Onderdeel5.VIN
  N12: Arduino_Nano_Shield_V1.D1/RX0, Onderdeel1.RX/GPIO1, Onderdeel2.RESET, Onderdeel3.RX/GPIO1, Onderdeel4.RX/GPIO1
  N13: Arduino_Nano_Shield_V1.D0/TX1, Onderdeel1.TX/GPIO0, Onderdeel2.RX/GPIO1, Onderdeel3.TX/GPIO0, Onderdeel4.TX/GPIO0
  N14: Arduino_Nano_Shield_V1.D13, Onderdeel1.SCK/D13/GPIO6, Onderdeel3.SCK/D13/GPIO6, Onderdeel4.SCK/D13/GPIO6, Onderdeel5.SCK/D13/GPIO6
  3V3: Arduino_Nano_Shield_V1.3V3, Onderdeel1.3V3, Onderdeel2.SCK/D13/GPIO6, Onderdeel3.3V3, Onderdeel4.3V3, Onderdeel5.3V3
  N15: Arduino_Nano_Shield_V1.REF, Onderdeel1.AREF, Onderdeel2.3V3, Onderdeel3.AREF, Onderdeel4.AREF, Onderdeel5.AREF
  N16: Arduino_Nano_Shield_V1.A0/D14, Onderdeel1.A0/D14/GPIO26, Onderdeel2.AREF, Onderdeel3.A0/D14/GPIO26, Onderdeel4.A0/D14/GPIO26, Onderdeel5.A0/D14/GPIO26
  N17: Arduino_Nano_Shield_V1.A1/D15, Onderdeel1.A1/D15/GPIO27, Onderdeel2.A0/D14/GPIO26, Onderdeel3.A1/D15/GPIO27, Onderdeel4.A1/D15/GPIO27, Onderdeel5.A1/D15/GPIO27
  N18: Arduino_Nano_Shield_V1.A2/D16, Onderdeel1.A2/D16/GPIO28, Onderdeel2.A1/D15/GPIO27, Onderdeel3.A2/D16/GPIO28, Onderdeel4.A2/D16/GPIO28, Onderdeel5.A2/D16/GPIO28
  N19: Arduino_Nano_Shield_V1.A3/D17, Onderdeel1.A3/D17/GPIO29, Onderdeel2.A2/D16/GPIO28, Onderdeel3.A3/D17/GPIO29, Onderdeel4.A3/D17/GPIO29, Onderdeel5.A3/D17/GPIO29
  N20: Arduino_Nano_Shield_V1.A4/D18/SDA, Onderdeel1.A4/D18/GPIO12, Onderdeel2.A3/D17/GPIO29, Onderdeel3.A4/D18/GPIO12, Onderdeel4.A4/D18/GPIO12, Onderdeel5.A4/D18/GPIO12
  N21: Arduino_Nano_Shield_V1.A5/D19/SCL, Onderdeel1.A5/D19/GPIO13, Onderdeel2.A4/D18/GPIO12, Onderdeel3.A5/D19/GPIO13, Onderdeel4.A5/D19/GPIO13, Onderdeel5.A5/D19/GPIO13
  N22: Arduino_Nano_Shield_V1.A6, Onderdeel1.A6/D20, Onderdeel2.A5/D19/GPIO13, Onderdeel3.A6/D20, Onderdeel4.A6/D20, Onderdeel5.A6/D20
  N23: Arduino_Nano_Shield_V1.A7, Onderdeel1.A7/D21, Onderdeel2.A6/D20, Onderdeel3.A7/D21, Onderdeel4.A7/D21, Onderdeel5.A7/D21
  5V: Arduino_Nano_Shield_V1.5V, Onderdeel1.5V, Onderdeel2.A7/D21, Onderdeel3.5V, Onderdeel4.5V, Onderdeel5.5V
  N24: Arduino_Nano_Shield_V1.RST#72, Onderdeel1.QSPI_CSn/RESET, Onderdeel2.5V, Onderdeel3.QSPI_CSn/RESET, Onderdeel4.QSPI_CSn/RESET, Onderdeel5.QSPI_CSn/RESET

notes:
  Let op dat D2,D3,D4 en D11 niet gebruikt kunnen worden, omdat deze gebruikt worden door de DC-motoren.

custom parts:
  Arduino Nano Shield V3: The Arduino Nano Shield is a compact and versatile accessory designed to simplify the development of Arduino Nano-based projects. This shield provides a convenient way to access all of the Nano's I/O pins, power connections, and additional features, making it ideal for prototyping and DIY electronics projects. Key Features: Pin Accessibility: Breaks out all 30 pins of the Arduino Nano to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
  Motor Shield Updated: Motor Shield
  I2C Updated: I2C
