# Fritzing sketch analog_irs_shield (saved by Fritzing 1.0.4)

parts:
  Shield1 = Arduino Nano Shield V3
  Onderdeel1 = Arduino Nano RP2040 Connect  # not connected
  IR1 = ky-033 [package=THT]
  IR19 = ky-033 [package=THT]

nets:
  N1: Shield1.A0/D14, IR1.pin1
  N2: Shield1.A1/D15, IR19.pin1
  N3: Shield1.3V3#93, IR1.pin4
  N4: Shield1.3V3#94, IR19.pin4
  N5: Shield1.GND#108, IR1.pin3
  N6: Shield1.GND#109, IR19.pin3

notes:
  Sensor links, rijtje van A0:
  blauw: AO naar A0 (binnen)
  rood: VCC naar 3V3 (midden)
  zwart: GND naar GND (buiten)
  Sensor rechts, rijtje van A1:
  blauw: AO naar A1 (binnen)
  rood: VCC naar 3V3 (midden)
  zwart: GND naar GND (buiten)
  DO blijft bij allebei leeg

custom parts:
  Arduino Nano Shield V3: The Arduino Nano Shield is a compact and versatile accessory designed to simplify the development of Arduino Nano-based projects. This shield provides a convenient way to access all of the Nano's I/O pins, power connections, and additional features, making it ideal for prototyping and DIY electronics projects. Key Features: Pin Accessibility: Breaks out all 30 pins of the Arduino Nano to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
  ky-033: KY-033 Line successor module with TCRT5000 and analog output.
