# Fritzing sketch golfbot (saved by Fritzing 1.0.6)

parts:
  Flitz_Shield1 = Flitz Shield
  M1 = Dagu DGServo 9g (Top view) [part_number=RS001B]
  A4 = ky-033 [package=THT]
  Composant3 = Arduino Nano (Rev3.0)

nets:
  N1: Flitz_Shield1.GND#11, A4.pin3
  N2: Flitz_Shield1.5V#26, A4.pin4
  VIN: Flitz_Shield1.VIN, Composant3.VIN
  N3: Flitz_Shield1.GND#33, Flitz_Shield1.GND#66, Composant3.GND
  N4: Flitz_Shield1.RST, Composant3.RESET
  N5: Flitz_Shield1.5V#37, Composant3.5V
  N6: Flitz_Shield1.A7, Composant3.A7
  N7: Flitz_Shield1.A6, Composant3.A6
  N8: Flitz_Shield1.A5/D19/SCL, Composant3.A5
  N9: Flitz_Shield1.A4/D18/SDA, Composant3.A4
  N10: Flitz_Shield1.A3/D17, Composant3.A3
  N11: Flitz_Shield1.A2/D16, Composant3.A2
  N12: Flitz_Shield1.A1/D15, Composant3.A1
  N13: Flitz_Shield1.A0/D14#52, A4.pin1
  N14: Flitz_Shield1.A0/D14#53, Composant3.A0
  N15: Flitz_Shield1.REF, Composant3.AREF
  3V3: Flitz_Shield1.3V3, Composant3.3V3
  N16: Flitz_Shield1.D13, Composant3.D13/SCK
  N17: Flitz_Shield1.D0/TX1, Composant3.D1/TX
  N18: Flitz_Shield1.D1/RX0, Composant3.D0/RX
  N19: Flitz_Shield1.D2, Composant3.D2
  N20: Flitz_Shield1.D3, Composant3.D3
  N21: Flitz_Shield1.D4, Composant3.D4
  N22: Flitz_Shield1.D5, Composant3.D5
  N23: Flitz_Shield1.D6, Composant3.D6
  N24: Flitz_Shield1.D7, Composant3.D7
  N25: Flitz_Shield1.D8, Composant3.D8
  N26: Flitz_Shield1.D9#82, Composant3.D9
  N27: Flitz_Shield1.D9#83, M1.pulse
  N28: Flitz_Shield1.D10, Composant3.D10
  N29: Flitz_Shield1.D11, Composant3.D11/MOSI
  N30: Flitz_Shield1.D12, Composant3.D12/MISO
  N31: Flitz_Shield1.5V#101, M1.vcc
  N32: Flitz_Shield1.GND#116, M1.gnd

custom parts:
  ky-033: KY-033 Line successor module with TCRT5000 and analog output.
