# Fritzing sketch shield_afstandssensor (saved by Fritzing 1.0.4)

parts:
  Shield1 = Arduino Nano Shield V3
  Onderdeel1 = Arduino Nano RP2040 Connect  # not connected
  Sensor1 = RCWL-1601 ultrasone afstandssensor

nets:
  GND: Shield1.GND, Sensor1.GND
  3V3: Shield1.3V3, Sensor1.VCC
  N1: Shield1.D8, Sensor1.ECHO
  N2: Shield1.D7, Sensor1.TRIG

notes:
  Rijtje van D8:
  groen: Echo naar D8 (binnen)
  rood: VCC naar 3V3 (midden)
  zwart: GND naar GND (buiten)
  Rijtje van D7:
  geel: Trig naar D7 (binnen)

custom parts:
  Arduino Nano Shield V3: The Arduino Nano Shield is a compact and versatile accessory designed to simplify the development of Arduino Nano-based projects. This shield provides a convenient way to access all of the Nano's I/O pins, power connections, and additional features, making it ideal for prototyping and DIY electronics projects. Key Features: Pin Accessibility: Breaks out all 30 pins of the Arduino Nano to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
  RCWL-1601 ultrasone afstandssensor: Ultrasone afstandssensor RCWL-1601 (werkt op 3,3 V). Getekend op basis van het HC-SR04 uit fritzing-parts.
