# Fritzing sketch shield_aluminiumtape (saved by Fritzing 1.0.4)

parts:
  Shield1 = Arduino Nano Shield V3
  Onderdeel1 = Arduino Nano RP2040 Connect  # not connected
  Tape1 = Aluminiumtape [package=buzzer-12mm-ns]

nets:
  N1: Shield1.GND, Tape1.draadje_1
  N2: Shield1.D5~, Tape1.draadje_2

notes:
  Rijtje van D5:
  blauw: van de tape naar D5 (binnen)
  zwart: van de tape naar GND (buiten)
  Raken allebei de draadjes de tape,
  dan wordt D5 0.

custom parts:
  Arduino Nano Shield V3: The Arduino Nano Shield is a compact and versatile accessory designed to simplify the development of Arduino Nano-based projects. This shield provides a convenient way to access all of the Nano's I/O pins, power connections, and additional features, making it ideal for prototyping and DIY electronics projects. Key Features: Pin Accessibility: Breaks out all 30 pins of the Arduino Nano to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
  Aluminiumtape: Een strook aluminiumtape op de vloer; twee draadjes die er allebei op liggen, zijn verbonden.
