# Fritzing sketch shield_battery_pack (saved by Fritzing 1.0.4)

parts:
  Shield1 = Arduino Nano Shield V3  # not connected
  Onderdeel1 = Arduino Nano RP2040 Connect  # not connected
  Adapter1 = Adapter voor de ronde bus [package=buzzer-12mm-ns]
  Batterijen1 = Batterijhouder 6x AA [package=buzzer-12mm-ns]

nets:
  N1: Adapter1.+, Batterijen1.+
  N2: Adapter1.-, Batterijen1.-

notes:
  Batterijhouder:
  rood: plus (+) naar + van de adapter
  zwart: min (-) naar - van de adapter
  De adapter gaat in de ronde bus
  van het shield.

custom parts:
  Arduino Nano Shield V3: The Arduino Nano Shield is a compact and versatile accessory designed to simplify the development of Arduino Nano-based projects. This shield provides a convenient way to access all of the Nano's I/O pins, power connections, and additional features, making it ideal for prototyping and DIY electronics projects. Key Features: Pin Accessibility: Breaks out all 30 pins of the Arduino Nano to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
  Adapter voor de ronde bus: Ronde stekker (5,5 mm) met een klemmetje voor + en -, voor de stroombus van het shield.
  Batterijhouder 6x AA: Batterijhouder voor zes AA-batterijen in serie, met een rode draad (+) en een zwarte draad (-).
