# Fritzing sketch shield_drukknop (saved by Fritzing 1.0.4)

parts:
  Shield1 = Arduino Nano Shield V3
  Onderdeel1 = Arduino Nano RP2040 Connect  # not connected
  Knop1 = Drukknop [package=buzzer-12mm-ns]

nets:
  N1: Shield1.GND, Knop1.pootje_2
  N2: Shield1.D7, Knop1.pootje_1

notes:
  Rijtje van D7:
  blauw: een pootje naar D7 (binnen)
  zwart: het andere pootje naar GND (buiten)

custom parts:
  Arduino Nano Shield V3: The Arduino Nano Shield is a compact and versatile accessory designed to simplify the development of Arduino Nano-based projects. This shield provides a convenient way to access all of the Nano's I/O pins, power connections, and additional features, making it ideal for prototyping and DIY electronics projects. Key Features: Pin Accessibility: Breaks out all 30 pins of the Arduino Nano to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
  Drukknop: Drukknop van 12 mm met twee pootjes: ingedrukt zijn ze met elkaar verbonden.
