# Fritzing sketch shield_ir_digitaal (saved by Fritzing 1.0.4)

parts:
  Shield1 = Arduino Nano Shield V3
  Onderdeel1 = Arduino Nano RP2040 Connect  # not connected
  IR1 = ky-033 [package=THT]

nets:
  N1: Shield1.A0/D14, IR1.pin2
  N2: Shield1.3V3, IR1.pin4
  N3: Shield1.GND, IR1.pin3

notes:
  Rijtje van D14:
  groen: DO naar D14 (binnen)
  rood: VCC naar 3V3 (midden)
  zwart: GND naar GND (buiten)
  AO blijft leeg

custom parts:
  Arduino Nano Shield V3: The Arduino Nano Shield is a compact and versatile accessory designed to simplify the development of Arduino Nano-based projects. This shield provides a convenient way to access all of the Nano's I/O pins, power connections, and additional features, making it ideal for prototyping and DIY electronics projects. Key Features: Pin Accessibility: Breaks out all 30 pins of the Arduino Nano to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
  ky-033: KY-033 Line successor module with TCRT5000 and analog output.
