# Fritzing sketch shield_joystick (saved by Fritzing 1.0.4)

parts:
  Shield1 = Arduino Nano Shield V3
  Onderdeel1 = Arduino Nano RP2040 Connect  # not connected
  Joystick1 = Joystickmodule KY-023 [package="5 mm [THT]"]

nets:
  N1: Shield1.A0/D14, Joystick1.SW
  N2: Shield1.A1/D15, Joystick1.VRy
  N3: Shield1.A2/D16, Joystick1.VRx
  3V3: Shield1.3V3, Joystick1.+5V
  GND: Shield1.GND, Joystick1.GND

notes:
  Joystick:
  groen: SW naar D14 (binnen), rijtje A0/D14
  geel: VRy naar A1 (binnen)
  oranje: VRx naar A2 (binnen)
  rood: +5V naar 3V3 (midden), rijtje A2
  zwart: GND naar GND (buiten), rijtje A2

custom parts:
  Arduino Nano Shield V3: The Arduino Nano Shield is a compact and versatile accessory designed to simplify the development of Arduino Nano-based projects. This shield provides a convenient way to access all of the Nano's I/O pins, power connections, and additional features, making it ideal for prototyping and DIY electronics projects. Key Features: Pin Accessibility: Breaks out all 30 pins of the Arduino Nano to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
  Joystickmodule KY-023: Joystick met twee potmeters (VRx en VRy) en een drukknop (SW).
