# Fritzing sketch shield_led (saved by Fritzing 1.0.4)

parts:
  Shield1 = Arduino Nano Shield V3
  Onderdeel1 = Arduino Nano RP2040 Connect  # not connected
  R1 = Resistor [resistance=220 package=THT]
  LED1 = LED - 5mm [color="Red (633nm)" package="5 mm [THT]"]

nets:
  N1: Shield1.GND, LED1.cathode
  N2: Shield1.D7, R1.Pin_1
  N3: R1.Pin_0, LED1.anode

notes:
  220 Ω
  Rijtje van D7:
  blauw: lange pin, via de weerstand,
  naar D7 (binnen)
  zwart: korte pin naar GND (buiten)

custom parts:
  Arduino Nano Shield V3: The Arduino Nano Shield is a compact and versatile accessory designed to simplify the development of Arduino Nano-based projects. This shield provides a convenient way to access all of the Nano's I/O pins, power connections, and additional features, making it ideal for prototyping and DIY electronics projects. Key Features: Pin Accessibility: Breaks out all 30 pins of the Arduino Nano to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
