# Fritzing sketch shield_meten (saved by Fritzing 1.0.4)

parts:
  Shield1 = Arduino Nano Shield V3
  Onderdeel1 = Arduino Nano RP2040 Connect  # not connected
  Multimeter1 = Multimeter (DC Voltage)

nets:
  N1: Shield1.A0/D14, Multimeter1.V_Probe
  N2: Shield1.GND, Multimeter1.COM_Probe

notes:
  Rijtje van D14 (A0/D14):
  rood: meetpen van VΩ naar D14 (binnen)
  zwart: meetpen van COM naar GND (buiten)
  Zet de multimeter op V met een streepje.

custom parts:
  Arduino Nano Shield V3: The Arduino Nano Shield is a compact and versatile accessory designed to simplify the development of Arduino Nano-based projects. This shield provides a convenient way to access all of the Nano's I/O pins, power connections, and additional features, making it ideal for prototyping and DIY electronics projects. Key Features: Pin Accessibility: Breaks out all 30 pins of the Arduino Nano to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
