# Fritzing sketch shield_oled_mux (saved by Fritzing 1.0.4)

parts:
  Shield1 = Arduino Nano Shield V3  # not connected
  Onderdeel1 = Arduino Nano RP2040 Connect  # not connected
  OLED1 = OLED-scherm 128x64 [package="5 mm [THT]"]
  Multiplexer1 = I2C Updated

nets:
  N1: OLED1.SCL, Multiplexer1.SCL
  N2: OLED1.SDA, Multiplexer1.SDA
  VCC: OLED1.VCC, Multiplexer1.VCC
  GND: OLED1.GND, Multiplexer1.GND

notes:
  Multiplexer, kanaal 7:
  blauw: SDA naar SDA
  geel: SCL naar SCL
  rood: VCC naar VCC
  zwart: GND naar GND
  De multiplexer steekt in de bus
  rechts op het shield.

custom parts:
  Arduino Nano Shield V3: The Arduino Nano Shield is a compact and versatile accessory designed to simplify the development of Arduino Nano-based projects. This shield provides a convenient way to access all of the Nano's I/O pins, power connections, and additional features, making it ideal for prototyping and DIY electronics projects. Key Features: Pin Accessibility: Breaks out all 30 pins of the Arduino Nano to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
  OLED-scherm 128x64: OLED-scherm van 128 x 64 pixels met de aansluitingen SCL, SDA, VCC en GND.
  I2C Updated: I2C
