# Fritzing sketch shield_oled_mux_ir (saved by Fritzing 1.0.4)

parts:
  Shield1 = Arduino Nano Shield V3
  Onderdeel1 = Arduino Nano RP2040 Connect  # not connected
  OLED1 = OLED-scherm 128x64 [package="5 mm [THT]"]
  Multiplexer1 = I2C Updated
  IR14 = ky-033 [package=THT]
  IR32 = ky-033 [package=THT]

nets:
  N1: Shield1.A0/D14, IR14.pin1
  N2: Shield1.A1/D15, IR32.pin1
  N3: Shield1.3V3#93, IR14.pin4
  N4: Shield1.3V3#94, IR32.pin4
  N5: Shield1.GND#108, IR14.pin3
  N6: Shield1.GND#109, IR32.pin3
  N7: OLED1.SCL, Multiplexer1.SCL
  N8: OLED1.SDA, Multiplexer1.SDA
  VCC: OLED1.VCC, Multiplexer1.VCC
  GND: OLED1.GND, Multiplexer1.GND

notes:
  Scherm op kanaal 7 van de multiplexer:
  blauw: SDA, geel: SCL, rood: VCC, zwart: GND
  IR-sensoren op A0 (links) en A1 (rechts):
  blauw: AO naar A0 of A1 (binnen)
  rood: VCC naar 3V3 (midden)
  zwart: GND naar GND (buiten)

custom parts:
  Arduino Nano Shield V3: The Arduino Nano Shield is a compact and versatile accessory designed to simplify the development of Arduino Nano-based projects. This shield provides a convenient way to access all of the Nano's I/O pins, power connections, and additional features, making it ideal for prototyping and DIY electronics projects. Key Features: Pin Accessibility: Breaks out all 30 pins of the Arduino Nano to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
  OLED-scherm 128x64: OLED-scherm van 128 x 64 pixels met de aansluitingen SCL, SDA, VCC en GND.
  I2C Updated: I2C
  ky-033: KY-033 Line successor module with TCRT5000 and analog output.
