# Fritzing sketch shield_potmeter (saved by Fritzing 1.0.4)

parts:
  Shield1 = Arduino Nano Shield V3
  Onderdeel1 = Arduino Nano RP2040 Connect  # not connected
  Potmeter1 = Draaipotmeter 10 kΩ [package="5 mm [THT]"]

nets:
  N1: Shield1.A0/D14, Potmeter1.loper
  N2: Shield1.3V3, Potmeter1.pootje_3
  N3: Shield1.GND, Potmeter1.pootje_1

notes:
  Rijtje van A0 (A0/D14):
  blauw: loper (middelste pootje) naar A0 (binnen)
  rood: pootje 3 naar 3V3 (midden)
  zwart: pootje 1 naar GND (buiten)

custom parts:
  Arduino Nano Shield V3: The Arduino Nano Shield is a compact and versatile accessory designed to simplify the development of Arduino Nano-based projects. This shield provides a convenient way to access all of the Nano's I/O pins, power connections, and additional features, making it ideal for prototyping and DIY electronics projects. Key Features: Pin Accessibility: Breaks out all 30 pins of the Arduino Nano to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
  Draaipotmeter 10 kΩ: Draaipotmeter met drie pootjes: de buitenste aan de plus en de min, de loper in het midden.
