# Fritzing sketch shield_tof (saved by Fritzing 1.0.4)

parts:
  Shield1 = Arduino Nano Shield V3
  Onderdeel1 = Arduino Nano RP2040 Connect  # not connected
  TOF1 = TOF-sensor [package="5 mm [THT]"]

nets:
  N1: Shield1.A4/D18/SDA, TOF1.SDA
  N2: Shield1.A5/D19/SCL, TOF1.SCL
  3V3: Shield1.3V3, TOF1.VCC
  GND: Shield1.GND, TOF1.GND

notes:
  TOF zonder multiplexer:
  blauw: SDA naar A4 (binnen)
  geel: SCL naar A5 (binnen)
  rood: VCC naar 3V3 (midden), rijtje A4
  zwart: GND naar GND (buiten), rijtje A4

custom parts:
  Arduino Nano Shield V3: The Arduino Nano Shield is a compact and versatile accessory designed to simplify the development of Arduino Nano-based projects. This shield provides a convenient way to access all of the Nano's I/O pins, power connections, and additional features, making it ideal for prototyping and DIY electronics projects. Key Features: Pin Accessibility: Breaks out all 30 pins of the Arduino Nano to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
  TOF-sensor: Afstandssensor (time of flight) van Leaphy met de pinnen SDA, SCL, VCC en GND.
