# Fritzing sketch shield_tof_mux (saved by Fritzing 1.0.4)

parts:
  Shield1 = Arduino Nano Shield V3  # not connected
  Onderdeel1 = Arduino Nano RP2040 Connect  # not connected
  TOF3 = TOF-sensor [package="5 mm [THT]"]
  Multiplexer1 = I2C Updated

nets:
  N1: TOF3.SDA, Multiplexer1.SDA
  N2: TOF3.SCL, Multiplexer1.SCL
  VCC: TOF3.VCC, Multiplexer1.VCC
  GND: TOF3.GND, Multiplexer1.GND

notes:
  Multiplexer, kanaal 7:
  blauw: SDA naar SDA
  geel: SCL naar SCL
  rood: VCC naar VCC
  zwart: GND naar GND
  De multiplexer steekt in de bus
  rechts op het shield.

custom parts:
  Arduino Nano Shield V3: The Arduino Nano Shield is a compact and versatile accessory designed to simplify the development of Arduino Nano-based projects. This shield provides a convenient way to access all of the Nano's I/O pins, power connections, and additional features, making it ideal for prototyping and DIY electronics projects. Key Features: Pin Accessibility: Breaks out all 30 pins of the Arduino Nano to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
  TOF-sensor: Afstandssensor (time of flight) van Leaphy met de pinnen SDA, SCL, VCC en GND.
  I2C Updated: I2C
