# Fritzing sketch shield_twee_tof_mux (saved by Fritzing 1.0.4)

parts:
  Shield1 = Arduino Nano Shield V3  # not connected
  Onderdeel1 = Arduino Nano RP2040 Connect  # not connected
  TOF3 = TOF-sensor [package="5 mm [THT]"]
  TOF12 = TOF-sensor [package="5 mm [THT]"]
  Multiplexer1 = I2C Updated

nets:
  N1: TOF3.SDA, Multiplexer1.SDA#15
  N2: TOF3.SCL, Multiplexer1.SCL#11
  N3: TOF3.VCC, Multiplexer1.VCC#7
  N4: TOF3.GND, Multiplexer1.GND#3
  N5: TOF12.SDA, Multiplexer1.SDA#35
  N6: TOF12.SCL, Multiplexer1.SCL#39
  N7: TOF12.VCC, Multiplexer1.VCC#43
  N8: TOF12.GND, Multiplexer1.GND#47

notes:
  TOF 1 op kanaal 0, TOF 2 op kanaal 7:
  blauw: SDA naar SDA
  geel: SCL naar SCL
  rood: VCC naar VCC
  zwart: GND naar GND
  Bij kanaal 0 staan de rijen andersom,
  daarom kruisen die draden.

custom parts:
  Arduino Nano Shield V3: The Arduino Nano Shield is a compact and versatile accessory designed to simplify the development of Arduino Nano-based projects. This shield provides a convenient way to access all of the Nano's I/O pins, power connections, and additional features, making it ideal for prototyping and DIY electronics projects. Key Features: Pin Accessibility: Breaks out all 30 pins of the Arduino Nano to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
  TOF-sensor: Afstandssensor (time of flight) van Leaphy met de pinnen SDA, SCL, VCC en GND.
  I2C Updated: I2C
