# Fritzing sketch shield_with_motors (saved by Fritzing 1.0.4)

parts:
  Shield1 = Arduino Nano Shield V3  # not connected
  Onderdeel1 = Arduino Nano RP2040 Connect  # not connected
  Motor_A = Getriebemotor
  Motor_B = Getriebemotor
  Motormodule1 = Motor Shield Updated

nets:
  N1: Motor_A.pin_1, Motormodule1.A-
  N2: Motor_A.pin_2, Motormodule1.A+
  N3: Motor_B.pin_1, Motormodule1.B-
  N4: Motor_B.pin_2, Motormodule1.B+

notes:
  Motor A: rood naar A+, zwart naar A-
  Motor B: rood naar B+, zwart naar B-
  De motormodule steekt in de bus
  links op het shield.

custom parts:
  Arduino Nano Shield V3: The Arduino Nano Shield is a compact and versatile accessory designed to simplify the development of Arduino Nano-based projects. This shield provides a convenient way to access all of the Nano's I/O pins, power connections, and additional features, making it ideal for prototyping and DIY electronics projects. Key Features: Pin Accessibility: Breaks out all 30 pins of the Arduino Nano to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
  Motor Shield Updated: Motor Shield
