# Fritzing sketch analog_irs_shield (saved by Fritzing 1.0.6)

parts:
  Onderdeel1 = Arduino Nano RP2040 Connect
  Onderdeel2 = Arduino Nano RP2040 Connect
  Onderdeel3 = Arduino Nano RP2040 Connect
  Onderdeel4 = Arduino Nano RP2040 Connect
  Onderdeel5 = Arduino Nano RP2040 Connect
  A2 = ky-033 [package=THT]
  Arduino_Nano_Shield_V1 = Arduino Nano Shield V3
  Onderdeel6 = Arduino Nano RP2040 Connect
  Part1 = Arduino Nano RP2040 Connect
  A3 = ky-033 [package=THT]
  Part2 = Arduino Nano RP2040 Connect

nets:
  N1: Onderdeel1.SCK/D13/GPIO6, Onderdeel3.SCK/D13/GPIO6, Onderdeel4.SCK/D13/GPIO6, Onderdeel5.SCK/D13/GPIO6, Arduino_Nano_Shield_V1.D13, Onderdeel6.SCK/D13/GPIO6, Part1.SCK/D13/GPIO6, Part2.SCK/D13/GPIO6
  3V3: Onderdeel1.3V3, Onderdeel2.SCK/D13/GPIO6, Onderdeel3.3V3, Onderdeel4.3V3, Onderdeel5.3V3, Arduino_Nano_Shield_V1.3V3#61, Onderdeel6.3V3, Part1.3V3, Part2.3V3
  N2: Onderdeel1.AREF, Onderdeel2.3V3, Onderdeel3.AREF, Onderdeel4.AREF, Onderdeel5.AREF, Arduino_Nano_Shield_V1.REF, Onderdeel6.AREF, Part1.AREF, Part2.AREF
  N3: Onderdeel1.A0/D14/GPIO26, Onderdeel2.AREF, Onderdeel3.A0/D14/GPIO26, Onderdeel4.A0/D14/GPIO26, Onderdeel5.A0/D14/GPIO26, Arduino_Nano_Shield_V1.A0/D14#63, Onderdeel6.A0/D14/GPIO26, Part1.A0/D14/GPIO26, Part2.A0/D14/GPIO26
  N4: Onderdeel1.A1/D15/GPIO27, Onderdeel2.A0/D14/GPIO26, Onderdeel3.A1/D15/GPIO27, Onderdeel4.A1/D15/GPIO27, Onderdeel5.A1/D15/GPIO27, Arduino_Nano_Shield_V1.A1/D15#64, Onderdeel6.A1/D15/GPIO27, Part1.A1/D15/GPIO27, Part2.A1/D15/GPIO27
  N5: Onderdeel1.A2/D16/GPIO28, Onderdeel2.A1/D15/GPIO27, Onderdeel3.A2/D16/GPIO28, Onderdeel4.A2/D16/GPIO28, Onderdeel5.A2/D16/GPIO28, Arduino_Nano_Shield_V1.A2/D16, Onderdeel6.A2/D16/GPIO28, Part1.A2/D16/GPIO28, Part2.A2/D16/GPIO28
  N6: Onderdeel1.A3/D17/GPIO29, Onderdeel2.A2/D16/GPIO28, Onderdeel3.A3/D17/GPIO29, Onderdeel4.A3/D17/GPIO29, Onderdeel5.A3/D17/GPIO29, Arduino_Nano_Shield_V1.A3/D17, Onderdeel6.A3/D17/GPIO29, Part1.A3/D17/GPIO29, Part2.A3/D17/GPIO29
  N7: Onderdeel1.A4/D18/GPIO12, Onderdeel2.A3/D17/GPIO29, Onderdeel3.A4/D18/GPIO12, Onderdeel4.A4/D18/GPIO12, Onderdeel5.A4/D18/GPIO12, Arduino_Nano_Shield_V1.A4/D18/SDA, Onderdeel6.A4/D18/GPIO12, Part1.A4/D18/GPIO12, Part2.A4/D18/GPIO12
  N8: Onderdeel1.A5/D19/GPIO13, Onderdeel2.A4/D18/GPIO12, Onderdeel3.A5/D19/GPIO13, Onderdeel4.A5/D19/GPIO13, Onderdeel5.A5/D19/GPIO13, Arduino_Nano_Shield_V1.A5/D19/SCL, Onderdeel6.A5/D19/GPIO13, Part1.A5/D19/GPIO13, Part2.A5/D19/GPIO13
  N9: Onderdeel1.A6/D20, Onderdeel2.A5/D19/GPIO13, Onderdeel3.A6/D20, Onderdeel4.A6/D20, Onderdeel5.A6/D20, Arduino_Nano_Shield_V1.A6, Onderdeel6.A6/D20, Part1.A6/D20, Part2.A6/D20
  N10: Onderdeel1.A7/D21, Onderdeel2.A6/D20, Onderdeel3.A7/D21, Onderdeel4.A7/D21, Onderdeel5.A7/D21, Arduino_Nano_Shield_V1.A7, Onderdeel6.A7/D21, Part1.A7/D21, Part2.A7/D21
  5V: Onderdeel1.5V, Onderdeel2.A7/D21, Onderdeel3.5V, Onderdeel4.5V, Onderdeel5.5V, Arduino_Nano_Shield_V1.5V, Onderdeel6.5V, Part1.5V, Part2.5V
  N11: Onderdeel1.QSPI_CSn/RESET, Onderdeel2.5V, Onderdeel3.QSPI_CSn/RESET, Onderdeel4.QSPI_CSn/RESET, Onderdeel5.QSPI_CSn/RESET, Arduino_Nano_Shield_V1.RST#72, Onderdeel6.QSPI_CSn/RESET, Part1.QSPI_CSn/RESET, Part2.QSPI_CSn/RESET
  GND: Onderdeel1.GND, Onderdeel2.QSPI_CSn/RESET, Onderdeel2.D2/GPIO25, Onderdeel3.GND, Onderdeel4.GND, Onderdeel5.GND, Arduino_Nano_Shield_V1.GND#56, Arduino_Nano_Shield_V1.GND#73, Onderdeel6.GND, Part1.GND, Part2.GND
  VIN: Onderdeel1.VIN, Onderdeel1.RESET, Onderdeel2.GND, Onderdeel3.VIN, Onderdeel3.RESET, Onderdeel4.VIN, Onderdeel4.RESET, Onderdeel5.VIN, Arduino_Nano_Shield_V1.RST#57, Arduino_Nano_Shield_V1.VIN, Onderdeel6.VIN, Onderdeel6.RESET, Part1.VIN, Part1.RESET, Part2.VIN, Part2.RESET
  N12: Onderdeel1.CIPO/D12/GPIO4, Onderdeel3.CIPO/D12/GPIO4, Onderdeel4.CIPO/D12/GPIO4, Arduino_Nano_Shield_V1.D12, Onderdeel6.CIPO/D12/GPIO4, Part1.CIPO/D12/GPIO4, Part2.CIPO/D12/GPIO4
  N13: Onderdeel1.COPI/D11/GPIO7, Onderdeel2.CIPO/D12/GPIO4, Onderdeel3.COPI/D11/GPIO7, Onderdeel4.COPI/D11/GPIO7, Arduino_Nano_Shield_V1.D11~, Onderdeel6.COPI/D11/GPIO7, Part1.COPI/D11/GPIO7, Part2.COPI/D11/GPIO7
  N14: Onderdeel1.D10/GPIO5, Onderdeel2.COPI/D11/GPIO7, Onderdeel3.D10/GPIO5, Onderdeel4.D10/GPIO5, Arduino_Nano_Shield_V1.D10~, Onderdeel6.D10/GPIO5, Part1.D10/GPIO5, Part2.D10/GPIO5
  N15: Onderdeel1.D9/GPIO21, Onderdeel2.D10/GPIO5, Onderdeel3.D9/GPIO21, Onderdeel4.D9/GPIO21, Arduino_Nano_Shield_V1.D9~, Onderdeel6.D9/GPIO21, Part1.D9/GPIO21, Part2.D9/GPIO21
  N16: Onderdeel1.D8/GPIO20, Onderdeel2.D9/GPIO21, Onderdeel3.D8/GPIO20, Onderdeel4.D8/GPIO20, Arduino_Nano_Shield_V1.D8, Onderdeel6.D8/GPIO20, Part1.D8/GPIO20, Part2.D8/GPIO20
  N17: Onderdeel1.D7/GPIO19, Onderdeel2.D8/GPIO20, Onderdeel3.D7/GPIO19, Onderdeel4.D7/GPIO19, Arduino_Nano_Shield_V1.D7, Onderdeel6.D7/GPIO19, Part1.D7/GPIO19, Part2.D7/GPIO19
  N18: Onderdeel1.D6/GPIO18, Onderdeel2.D7/GPIO19, Onderdeel3.D6/GPIO18, Onderdeel4.D6/GPIO18, Arduino_Nano_Shield_V1.D6~, Onderdeel6.D6/GPIO18, Part1.D6/GPIO18, Part2.D6/GPIO18
  N19: Onderdeel1.D5/GPIO17, Onderdeel2.D6/GPIO18, Onderdeel3.D5/GPIO17, Onderdeel4.D5/GPIO17, Arduino_Nano_Shield_V1.D5~, Onderdeel6.D5/GPIO17, Part1.D5/GPIO17, Part2.D5/GPIO17
  N20: Onderdeel1.D4/GPIO16, Onderdeel2.D5/GPIO17, Onderdeel3.D4/GPIO16, Onderdeel4.D4/GPIO16, Arduino_Nano_Shield_V1.D4, Onderdeel6.D4/GPIO16, Part1.D4/GPIO16, Part2.D4/GPIO16
  N21: Onderdeel1.D3/GPIO15, Onderdeel2.D4/GPIO16, Onderdeel3.D3/GPIO15, Onderdeel4.D3/GPIO15, Arduino_Nano_Shield_V1.D3~, Onderdeel6.D3/GPIO15, Part1.D3/GPIO15, Part2.D3/GPIO15
  N22: Onderdeel1.D2/GPIO25, Onderdeel2.D3/GPIO15, Onderdeel3.D2/GPIO25, Onderdeel4.D2/GPIO25, Arduino_Nano_Shield_V1.D2, Onderdeel6.D2/GPIO25, Part1.D2/GPIO25, Part2.D2/GPIO25
  N23: Onderdeel1.RX/GPIO1, Onderdeel2.RESET, Onderdeel3.RX/GPIO1, Onderdeel4.RX/GPIO1, Arduino_Nano_Shield_V1.D1/RX0, Onderdeel6.RX/GPIO1, Part1.RX/GPIO1, Part2.RX/GPIO1
  N24: Onderdeel1.TX/GPIO0, Onderdeel2.RX/GPIO1, Onderdeel3.TX/GPIO0, Onderdeel4.TX/GPIO0, Arduino_Nano_Shield_V1.D0/TX1, Onderdeel6.TX/GPIO0, Part1.TX/GPIO0, Part2.TX/GPIO0
  N25: A2.pin1, Arduino_Nano_Shield_V1.A0/D14#78
  N26: A2.pin3, Arduino_Nano_Shield_V1.GND#108
  N27: A2.pin4, Arduino_Nano_Shield_V1.3V3#93
  N28: Arduino_Nano_Shield_V1.A1/D15#79, A3.pin1
  N29: Arduino_Nano_Shield_V1.3V3#94, A3.pin4
  N30: Arduino_Nano_Shield_V1.GND#109, A3.pin3

notes:
  Voor de blauwe kun je een willekeurige kleur pakken.
  Pak de rode en zwarte combinatie (die aan elkaar vast zitten)

custom parts:
  ky-033: KY-033 Line successor module with TCRT5000 and analog output.
  Arduino Nano Shield V3: The Arduino Nano Shield is a compact and versatile accessory designed to simplify the development of Arduino Nano-based projects. This shield provides a convenient way to access all of the Nano's I/O pins, power connections, and additional features, making it ideal for prototyping and DIY electronics projects. Key Features: Pin Accessibility: Breaks out all 30 pins of the Arduino Nano to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
