# Fritzing sketch shield_with_motors (saved by Fritzing 1.0.4)

parts:
  Arduino_Nano_Shield_V1 = Arduino Nano Shield V3
  Onderdeel1 = Arduino Nano RP2040 Connect
  Motor_Shield1 = Motor Shield Updated  # not connected
  M1 = Getriebemotor  # not connected
  M2 = Getriebemotor  # not connected

nets:
  N1: Arduino_Nano_Shield_V1.D12, Onderdeel1.CIPO/D12/GPIO4
  N2: Arduino_Nano_Shield_V1.D11~, Onderdeel1.COPI/D11/GPIO7
  N3: Arduino_Nano_Shield_V1.D10~, Onderdeel1.D10/GPIO5
  N4: Arduino_Nano_Shield_V1.D9~, Onderdeel1.D9/GPIO21
  N5: Arduino_Nano_Shield_V1.D8, Onderdeel1.D8/GPIO20
  N6: Arduino_Nano_Shield_V1.D7, Onderdeel1.D7/GPIO19
  N7: Arduino_Nano_Shield_V1.D6~, Onderdeel1.D6/GPIO18
  N8: Arduino_Nano_Shield_V1.D5~, Onderdeel1.D5/GPIO17
  N9: Arduino_Nano_Shield_V1.D4, Onderdeel1.D4/GPIO16
  N10: Arduino_Nano_Shield_V1.D3~, Onderdeel1.D3/GPIO15
  N11: Arduino_Nano_Shield_V1.D2, Onderdeel1.D2/GPIO25
  GND: Arduino_Nano_Shield_V1.GND, Onderdeel1.GND
  N12: Arduino_Nano_Shield_V1.RST#57, Onderdeel1.RESET
  N13: Arduino_Nano_Shield_V1.D1/RX0, Onderdeel1.RX/GPIO1
  N14: Arduino_Nano_Shield_V1.D0/TX1, Onderdeel1.TX/GPIO0
  N15: Arduino_Nano_Shield_V1.D13, Onderdeel1.SCK/D13/GPIO6
  3V3: Arduino_Nano_Shield_V1.3V3, Onderdeel1.3V3
  N16: Arduino_Nano_Shield_V1.REF, Onderdeel1.AREF
  N17: Arduino_Nano_Shield_V1.A0/D14, Onderdeel1.A0/D14/GPIO26
  N18: Arduino_Nano_Shield_V1.A1/D15, Onderdeel1.A1/D15/GPIO27
  N19: Arduino_Nano_Shield_V1.A2/D16, Onderdeel1.A2/D16/GPIO28
  N20: Arduino_Nano_Shield_V1.A3/D17, Onderdeel1.A3/D17/GPIO29
  N21: Arduino_Nano_Shield_V1.A4/D18/SDA, Onderdeel1.A4/D18/GPIO12
  N22: Arduino_Nano_Shield_V1.A5/D19/SCL, Onderdeel1.A5/D19/GPIO13
  N23: Arduino_Nano_Shield_V1.A6, Onderdeel1.A6/D20
  N24: Arduino_Nano_Shield_V1.A7, Onderdeel1.A7/D21
  5V: Arduino_Nano_Shield_V1.5V, Onderdeel1.5V
  N25: Arduino_Nano_Shield_V1.RST#72, Onderdeel1.QSPI_CSn/RESET
  VIN: Arduino_Nano_Shield_V1.VIN, Onderdeel1.VIN

custom parts:
  Arduino Nano Shield V3: The Arduino Nano Shield is a compact and versatile accessory designed to simplify the development of Arduino Nano-based projects. This shield provides a convenient way to access all of the Nano's I/O pins, power connections, and additional features, making it ideal for prototyping and DIY electronics projects. Key Features: Pin Accessibility: Breaks out all 30 pins of the Arduino Nano to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
  Motor Shield Updated: Motor Shield
